// Logisim project Main bus.circ as structural Verilog: 1 circuit, main circuit Main bus
module Main_bus (
  input  in_1,
  input  in_2
);

  wire [6:0] keyboard_1_data;
  wire [7:0] controlled_buffer_2_out;
  wire [15:0] Accumulator_register_q, controlled_buffer_1_out, controlled_buffer_3_out,
       controlled_buffer_4_out, Input_register_q;

  Counter #(.width(16), .max('hffff)) Program_counter ();  // open: load, D, count, Q, carry, clk, clr
  Register #(.width(16)) Memory_access_register (.D(controlled_buffer_1_out));  // open: en, Q, clk, clr
  Controlled_Buffer #(.width(16)) controlled_buffer_1 (.out(controlled_buffer_1_out));  // open: in, en
  Controlled_Buffer #(.width(8)) controlled_buffer_2 (.out(controlled_buffer_2_out));  // open: in, en
  Register Instruction_register (.D(controlled_buffer_2_out));  // open: en, Q, clk, clr
  RAM ram_1 ();  // open: addr, data, sel, clk, ld, clr
  ROM rom_1 ();  // open: addr, data, sel
  Keyboard keyboard_1 (.clk(in_1), .clr(in_2), .data(keyboard_1_data));  // open: re, avail
  Controlled_Buffer #(.width(16)) controlled_buffer_3 (.out(controlled_buffer_3_out));  // open: in, en
  Controlled_Buffer #(.width(16)) controlled_buffer_4 (.out(controlled_buffer_4_out));  // open: in, en
  TTY tty_1 (.data(keyboard_1_data), .clk(in_1), .clr(in_2));  // open: we
  Register #(.width(16)) Accumulator_register (
    .D(controlled_buffer_3_out), .Q(Accumulator_register_q));  // open: en, clk, clr
  Controlled_Buffer #(.width(16)) controlled_buffer_5 (.in(Accumulator_register_q));  // open: out, en
  Register #(.width(16)) Input_register (.D(controlled_buffer_4_out), .Q(Input_register_q));  // open: en, clk, clr
  Controlled_Buffer #(.width(16)) controlled_buffer_6 (.in(Input_register_q));  // open: out, en
  Register #(.width(16)) Output_register ();  // open: D, en, Q, clk, clr

  // Notes on the sheet:
  //   RAM for storage
  //   ROM for control matrix
  //   ALU
endmodule
